// Logisim project div_by_6__4_bit.circ as structural Verilog: 1 circuit, main circuit main
module main (
  input  A,
  input  B,
  input  C,
  input  D,
  output Z
);

  wire and_1_out, and_2_out, nor_1_out, not_1_out, xor_1_out, xor_2_out, xor_3_out, xor_4_out;

  xor xor_1 (xor_1_out, A, C);
  and and_1 (and_1_out, B, D);
  not not_1 (not_1_out, D);
  and and_2 (and_2_out, A, C);
  xor xor_2 (xor_2_out, B, D);
  xor xor_3 (xor_3_out, xor_1_out, xor_2_out);
  xor xor_4 (xor_4_out, and_2_out, and_1_out);
  nor nor_1 (nor_1_out, xor_3_out, xor_4_out);
  and and_3 (Z, nor_1_out, not_1_out);
endmodule
